// Logisim project RV32_IM_ROM.circ as structural Verilog: 4 circuits, main circuit main
module main (
);

  wire and_1_out, CLK, comparator_1_eq, RAM_WRITE_EN;
  wire [31:0] RAM_ADDR, RAM_READ_DATA, RAM_WRITE_DATA, ROM_ADDR, ROM_DATA, shifter_1_out, shifter_2_out;

  // Probe on RAM_ADDR
  CPU cpu_1 (
    .Outputs(RAM_ADDR), .out_5(RAM_WRITE_DATA), .out_6(RAM_WRITE_EN), .out_7(ROM_ADDR),
    .Inputs(RAM_READ_DATA), .in_2(ROM_DATA), .in_3(CLK));
  Comparator #(.width(18)) comparator_1 (.a(RAM_ADDR[31:14]), .b(18'h20000), .eq(comparator_1_eq));  // open: gt, lt
  and and_1 (and_1_out, comparator_1_eq, RAM_WRITE_EN);
  Shifter #(.shift("lr"), .width(32)) shifter_1 (.in(RAM_ADDR), .\dist (5'b00010), .out(shifter_1_out));
  // Probe on RAM_WRITE_DATA
  RAM #(.addrWidth(12), .dataWidth(32), .enables("line")) ram_1 (
    .addr(shifter_1_out[11:0]), .we(and_1_out), .clk(CLK), .din(RAM_WRITE_DATA), .dout(RAM_READ_DATA));
  Clock u_clk (.out(CLK));
  // Probe on ROM_ADDR
  Shifter #(.shift("lr"), .width(32)) shifter_2 (.in(ROM_ADDR), .\dist (5'b00010), .out(shifter_2_out));
  ROM #(.addrWidth(12), .dataWidth(32)) rom_1 (.addr(shifter_2_out[11:0]), .data(ROM_DATA));
  // Probe on ROM_DATA

  // Notes on the sheet:
  //   CPU
  //   RAM
  //   verif plage RAM
  //   test bits 31..14
  //   Décodage d'adresse RAM
  //   plage 0x80000000 à 0x80003FFF (16Kb)
  //   div/4 car mots de 32 bits
  //   4K x 32 => 16KB
  //   Version modifiée à partir du design initial "RISC-V Bilgisayar (RV32IM)" d'Emin Fedar (2020)
  //   ROM
  //   32 bit alignment
endmodule

module CPU (
  input  [31:0] Inputs,
  input  [31:0] in_2,
  input  in_3,
  output [31:0] Outputs,
  output [31:0] out_5,
  output out_6,
  output [31:0] out_7
);

  wire branchALU, branchRel, branchRelCond, immRs2, PCRs1, rom_3_data, wePC, weRd;
  wire [1:0] WB_Sel;
  wire [2:0] Imm_Sel;
  wire [3:0] AluOp, NZVC;
  wire [5:0] rom_1_data;
  wire [7:0] RAM_READ_DATA_BYTE;
  wire [15:0] RAM_READ_DATA_HW;
  wire [31:0] bit_extender_1_out, bit_extender_2_out, bit_extender_3_out, bit_extender_4_out,
       bit_extender_5_out, bit_extender_6_out, bit_extender_7_out, bit_extender_8_out, Imm_Value,
       multiplexer_1_out, multiplexer_2_out, multiplexer_3_out, multiplexer_4_out, PCOffsetNext,
       RAM_READ_DATA_WITH_TYPE, RAM_WRITE_DATA_B, RAM_WRITE_DATA_HW, Rd_DATA, Rs1_DATA, Rs2_DATA;

  // Probe on in_2[19:15]
  // Probe on Rs1_DATA
  REGISTERS registers_1 (
    .Outputs(Rs1_DATA), .out_8(Rs2_DATA), .in_5(weRd), .in_6(in_3), .in_1(in_2[19:15]), .in_2(in_2[24:20]),
    .in_3(in_2[11:7]), .in_4(Rd_DATA));
  // Probe on in_2[11:7]
  // Probe on Rd_DATA
  Multiplexer #(.width(32)) multiplexer_1 (.in0(32'h4), .in1(Imm_Value), .out(multiplexer_1_out), .sel(branchRel));
  Multiplexer #(.width(32)) multiplexer_2 (.in0(out_7), .in1(Rs1_DATA), .out(multiplexer_2_out), .sel(PCRs1));
  Multiplexer #(.width(32)) multiplexer_3 (.in0(Imm_Value), .in1(Rs2_DATA), .out(multiplexer_3_out), .sel(immRs2));
  // Probe on PCOffsetNext
  Adder #(.width(32)) adder_1 (.a(out_7), .b(multiplexer_1_out), .out(PCOffsetNext));  // open: cin, cout
  ALU alu_1 (.Outputs(Outputs), .out_5(NZVC), .in_1(multiplexer_2_out), .in_2(multiplexer_3_out), .in_3(AluOp));
  // Probe on in_2[24:20]
  Multiplexer #(.width(32)) multiplexer_4 (.in0(PCOffsetNext), .in1(Outputs), .out(multiplexer_4_out), .sel(branchALU));
  // Probe on NZVC
  // Probe on Outputs
  // Probe on AluOp
  // Probe on Rd_DATA
  Multiplexer #(.select(2), .width(32)) multiplexer_5 (
    .in0(Outputs), .in1(RAM_READ_DATA_WITH_TYPE), .in2(PCOffsetNext), .out(Rd_DATA), .sel(WB_Sel));  // open: in3
  // Probe on WB_Sel
  // Probe on Rs2_DATA
  Register #(.width(32)) PC (.D(multiplexer_4_out), .en(wePC), .clk(in_3), .Q(out_7));  // open: clr
  assign bit_extender_1_out = {{20{in_2[31]}}, in_2[31:20]};  // Bit_Extender bit_extender_1
  assign bit_extender_2_out = {{20{in_2[31]}}, {in_2[31:25], in_2[11:7]}};  // Bit_Extender bit_extender_2
  assign bit_extender_3_out = {{19{in_2[31]}}, {in_2[31], in_2[7], in_2[30:25], in_2[11:8], 1'b0}};  // Bit_Extender bit_extender_3
  assign bit_extender_4_out = {{11{in_2[31]}}, {in_2[31], in_2[19:12], in_2[20], in_2[30:21], 1'b0}};  // Bit_Extender bit_extender_4
  Multiplexer #(.select(3), .width(32)) multiplexer_6 (
    .in0(bit_extender_1_out), .in1(bit_extender_2_out), .in2(bit_extender_3_out),
    .in3({in_2[31:12], {12{1'b0}}}), .in4(bit_extender_4_out), .out(Imm_Value), .sel(Imm_Sel));  // open: in5, in6, in7
  // Probe on Imm_Value
  assign bit_extender_5_out = {{24{RAM_READ_DATA_BYTE[7]}}, RAM_READ_DATA_BYTE};  // Bit_Extender bit_extender_5
  assign bit_extender_6_out = {{16{RAM_READ_DATA_HW[15]}}, RAM_READ_DATA_HW};  // Bit_Extender bit_extender_6
  assign bit_extender_7_out = {{24{1'b0}}, RAM_READ_DATA_BYTE};  // Bit_Extender bit_extender_7
  assign bit_extender_8_out = {{16{1'b0}}, RAM_READ_DATA_HW};  // Bit_Extender bit_extender_8
  // Probe on Outputs
  Multiplexer #(.select(2), .width(8)) multiplexer_7 (
    .in0(Inputs[7:0]), .in1(Inputs[15:8]), .in2(Inputs[23:16]), .in3(Inputs[31:24]),
    .out(RAM_READ_DATA_BYTE), .sel(Outputs[1:0]));
  Multiplexer #(.width(16)) multiplexer_8 (
    .in0(Inputs[15:0]), .in1(Inputs[31:16]), .out(RAM_READ_DATA_HW), .sel(Outputs[1]));
  ROM #(.addrWidth(9), .dataWidth(6)) rom_1 (.addr({in_2[6:2], in_2[30], in_2[14:12]}), .data(rom_1_data));
  ROM #(.addrWidth(6), .dataWidth(16)) rom_2 (
    .addr(rom_1_data),
    .data({branchALU, out_6, WB_Sel, AluOp, branchRelCond, immRs2, PCRs1, weRd, Imm_Sel, wePC}));
  // Probe on {in_2[14:12], NZVC}
  ROM #(.addrWidth(7), .dataWidth(1)) rom_3 (.addr({in_2[14:12], NZVC}), .data(rom_3_data));
  Multiplexer #(.select(3), .width(32)) multiplexer_9 (
    .in0(bit_extender_5_out), .in1(bit_extender_6_out), .in2(Inputs), .in4(bit_extender_7_out),
    .in5(bit_extender_8_out), .out(RAM_READ_DATA_WITH_TYPE), .sel(in_2[14:12]));  // open: in3, in6, in7
  // Probe on RAM_READ_DATA_WITH_TYPE
  // Probe on rom_1_data
  Multiplexer #(.select(3), .width(32)) multiplexer_10 (
    .in0(RAM_WRITE_DATA_B), .in1(RAM_WRITE_DATA_HW), .in2(Rs2_DATA), .out(out_5), .sel(in_2[14:12]));  // open: in3, in4, in5, in6, in7
  // Probe on in_2[14:12]
  Multiplexer #(.width(32)) multiplexer_11 (
    .in0({Inputs[31:16], Rs2_DATA[15:0]}), .in1({Rs2_DATA[15:0], Inputs[15:0]}), .out(RAM_WRITE_DATA_HW),
    .sel(Outputs[1]));
  Multiplexer #(.select(2), .width(32)) multiplexer_12 (
    .in0({Inputs[31:8], Rs2_DATA[7:0]}), .in1({Inputs[31:16], Rs2_DATA[7:0], Inputs[7:0]}),
    .in2({Inputs[31:24], Rs2_DATA[7:0], Inputs[15:0]}), .in3({Rs2_DATA[7:0], Inputs[23:0]}),
    .out(RAM_WRITE_DATA_B), .sel(Outputs[1:0]));
  // Probe on out_5

  // Other names for the same wires on the sheet: INSTRUCTION[31:0] = in_2; Rs2[4:0] = in_2[24:20];
  //   FUNCT7[6:0] = in_2[31:25]; Rs1[4:0] = in_2[19:15]; Rd[4:0] = in_2[11:7]; OPCODE[6:0] = in_2[6:0];
  //   FUNCT3[2:0] = in_2[14:12]; RAM_WRITE_EN = out_6; RAM_READ_DATA[31:0] = Inputs; Rs2_DATA_B[7:0] = Rs2_DATA[7:0];
  //   Rs2_DATA_HW[15:0] = Rs2_DATA[15:0]; CLK = in_3; INSTRUCTION_ADDR[31:0] = out_7; PC[31:0] = out_7;
  //   ALU_OUT[31:0] = Outputs; RAM_ADDR[31:0] = Outputs; RAM_WRITE_DATA[31:0] = out_5

  // Notes on the sheet:
  //   I/O
  //   1.FETCH
  //   3. EXECUTE
  //   5. WRITE BACK
  //   TODO!
  //   appelé ROM_ADDR dans le main
  //   RS1
  //   RD
  //   RS2
  //   appelé ROM_DATA dans le main
  //   2.DECODE
  //   R-Type
  //   I-Type
  //   S-Type
  //   B-Type
  //   U-Type
  //   J-Type
  //   U-Type
  //   get: (imm << 12)
  //   4. MEMORY
  //   voir spec: riscv-spec-20191213
  //   p.16 - fig 2.3
  //   Extract word/half word and byte from ram data
  //   decodage des formats d'instruction
  //   p.17 - fig 2.4
  //   attention: jalr utilise le I-type!!
  //   Select correct byte from memory
  //   Select correct byte from memory
  //   decodage des immédiats
  //   voir spec: riscv-spec-20191213
  //   byte sign-extended
  //   half word sign-extended
  //   word
  //   byte unsigned
  //   half word unsigned
  //   contents of rom_1 (hex, n*v repeats v):
  //   14 15 16 0 17 18 0 0 14 15 16 0 17 18 50*0 b f 12 13 c 10 d e b 0 12 13 c 11 d e 16*25 32*0 19 1a 1b
  //   5*0 19 1a 1b 53*0 1 6 9 a 3 7 4 5 2 4*0 8 0 0 16*24 160*0 1c 1d 0 0 1e 1f 20 21 1c 1d 0 0 1e 1f 20
  //   21 23 7*0 23 23*0 16*22 16*26
  //   TODO!
  //   TODO!
  //   Allow to write a word/half word/ byte onto memory
  //   id d'instruction
  //   TODO!
  //   - wePC => 1bit
  //   - imm_sel => 3 bits
  //   - weRd => 1 bit
  //   - PCRs1 => 1 bit
  //   - immRs2 => 1 bit
  //   - branchRelCond => 1bit
  //   - aluOp => 4 bits
  //   - wbSel => 2bits
  //   - memWrite => 1bit
  //   - branchALU => 1bit
  //   control signals
endmodule

module REGISTERS (
  input  [4:0] in_1,
  input  [4:0] in_2,
  input  [4:0] in_3,
  input  [31:0] in_4,
  input  in_5,
  input  in_6,
  output [31:0] Outputs,
  output [31:0] out_8
);

  wire WE_1, WE_2, WE_3, WE_4, WE_5, WE_6, WE_7, WE_8, WE_9, WE_10, WE_11, WE_12, WE_13, WE_14, WE_15, WE_16,
       WE_17, WE_18, WE_19, WE_20, WE_21, WE_22, WE_23, WE_24, WE_25, WE_26, WE_27, WE_28, WE_29, WE_30,
       WE_31;
  wire [31:0] in_r1, in_r2, in_r3, in_r4, in_r5, in_r6, in_r7, in_r8, in_r9, in_r10, in_r11, in_r12, in_r13,
       in_r14, in_r15, in_r16, in_r17, in_r18, in_r19, in_r20, in_r21, in_r22, in_r23, in_r24, in_r25,
       in_r26, in_r27, in_r28, in_r29, in_r30, in_r31, out_r1, out_r2, out_r3, out_r4, out_r5, out_r6,
       out_r7, out_r8, out_r9, out_r10, out_r11, out_r12, out_r13, out_r14, out_r15, out_r16, out_r17,
       out_r18, out_r19, out_r20, out_r21, out_r22, out_r23, out_r24, out_r25, out_r26, out_r27, out_r28,
       out_r29, out_r30, out_r31;

  Register #(.width(32)) x1_ra (.D(in_r1), .en(WE_1), .clk(in_6), .Q(out_r1));  // open: clr
  Register #(.width(32)) x9_s1 (.D(in_r9), .en(WE_9), .clk(in_6), .Q(out_r9));  // open: clr
  Register #(.width(32)) x17_a7 (.D(in_r17), .en(WE_17), .clk(in_6), .Q(out_r17));  // open: clr
  Register #(.width(32)) x25_s9 (.D(in_r25), .en(WE_25), .clk(in_6), .Q(out_r25));  // open: clr
  Register #(.width(32)) x2_sp (.D(in_r2), .en(WE_2), .clk(in_6), .Q(out_r2));  // open: clr
  Register #(.width(32)) x10_a0 (.D(in_r10), .en(WE_10), .clk(in_6), .Q(out_r10));  // open: clr
  Register #(.width(32)) x18_s2 (.D(in_r18), .en(WE_18), .clk(in_6), .Q(out_r18));  // open: clr
  Register #(.width(32)) x26_s10 (.D(in_r26), .en(WE_26), .clk(in_6), .Q(out_r26));  // open: clr
  Register #(.width(32)) x3_gp (.D(in_r3), .en(WE_3), .clk(in_6), .Q(out_r3));  // open: clr
  Register #(.width(32)) x11_a1 (.D(in_r11), .en(WE_11), .clk(in_6), .Q(out_r11));  // open: clr
  Register #(.width(32)) x19_s3 (.D(in_r19), .en(WE_19), .clk(in_6), .Q(out_r19));  // open: clr
  Register #(.width(32)) x27_s11 (.D(in_r27), .en(WE_27), .clk(in_6), .Q(out_r27));  // open: clr
  Multiplexer #(.select(5), .width(32)) multiplexer_1 (
    .in0({32{1'b0}}), .in1(out_r1), .in2(out_r2), .in3(out_r3), .in4(out_r4), .in5(out_r5), .in6(out_r6),
    .in7(out_r7), .in8(out_r8), .in9(out_r9), .in10(out_r10), .in11(out_r11), .in12(out_r12), .in13(out_r13),
    .in14(out_r14), .in15(out_r15), .in16(out_r16), .in17(out_r17), .in18(out_r18), .in19(out_r19),
    .in20(out_r20), .in21(out_r21), .in22(out_r22), .in23(out_r23), .in24(out_r24), .in25(out_r25),
    .in26(out_r26), .in27(out_r27), .in28(out_r28), .in29(out_r29), .in30(out_r30), .in31(out_r31),
    .out(Outputs), .sel(in_1));
  Register #(.width(32)) x4_tp (.D(in_r4), .en(WE_4), .clk(in_6), .Q(out_r4));  // open: clr
  Register #(.width(32)) x12_a2 (.D(in_r12), .en(WE_12), .clk(in_6), .Q(out_r12));  // open: clr
  Register #(.width(32)) x20_s4 (.D(in_r20), .en(WE_20), .clk(in_6), .Q(out_r20));  // open: clr
  Register #(.width(32)) x28_t3 (.D(in_r28), .en(WE_28), .clk(in_6), .Q(out_r28));  // open: clr
  Multiplexer #(.select(5), .width(32)) multiplexer_2 (
    .in0({32{1'b0}}), .in1(out_r1), .in2(out_r2), .in3(out_r3), .in4(out_r4), .in5(out_r5), .in6(out_r6),
    .in7(out_r7), .in8(out_r8), .in9(out_r9), .in10(out_r10), .in11(out_r11), .in12(out_r12), .in13(out_r13),
    .in14(out_r14), .in15(out_r15), .in16(out_r16), .in17(out_r17), .in18(out_r18), .in19(out_r19),
    .in20(out_r20), .in21(out_r21), .in22(out_r22), .in23(out_r23), .in24(out_r24), .in25(out_r25),
    .in26(out_r26), .in27(out_r27), .in28(out_r28), .in29(out_r29), .in30(out_r30), .in31(out_r31),
    .out(out_8), .sel(in_2));
  Register #(.width(32)) x5_t0 (.D(in_r5), .en(WE_5), .clk(in_6), .Q(out_r5));  // open: clr
  Register #(.width(32)) x13_a3 (.D(in_r13), .en(WE_13), .clk(in_6), .Q(out_r13));  // open: clr
  Register #(.width(32)) x21_s5 (.D(in_r21), .en(WE_21), .clk(in_6), .Q(out_r21));  // open: clr
  Register #(.width(32)) x29_t4 (.D(in_r29), .en(WE_29), .clk(in_6), .Q(out_r29));  // open: clr
  Register #(.width(32)) x6_t1 (.D(in_r6), .en(WE_6), .clk(in_6), .Q(out_r6));  // open: clr
  Register #(.width(32)) x14_a4 (.D(in_r14), .en(WE_14), .clk(in_6), .Q(out_r14));  // open: clr
  Register #(.width(32)) x22_s6 (.D(in_r22), .en(WE_22), .clk(in_6), .Q(out_r22));  // open: clr
  Register #(.width(32)) x30_t5 (.D(in_r30), .en(WE_30), .clk(in_6), .Q(out_r30));  // open: clr
  Demultiplexer #(.enable("true"), .select(5), .width(32)) demultiplexer_1 (
    .out1(in_r1), .out2(in_r2), .out3(in_r3), .out4(in_r4), .out5(in_r5), .out6(in_r6), .out7(in_r7),
    .out8(in_r8), .out9(in_r9), .out10(in_r10), .out11(in_r11), .out12(in_r12), .out13(in_r13),
    .out14(in_r14), .out15(in_r15), .out16(in_r16), .out17(in_r17), .out18(in_r18), .out19(in_r19),
    .out20(in_r20), .out21(in_r21), .out22(in_r22), .out23(in_r23), .out24(in_r24), .out25(in_r25),
    .out26(in_r26), .out27(in_r27), .out28(in_r28), .out29(in_r29), .out30(in_r30), .out31(in_r31),
    .in(in_4), .sel(in_3), .en(in_5));  // open: out0
  Register #(.width(32)) x7_t2 (.D(in_r7), .en(WE_7), .clk(in_6), .Q(out_r7));  // open: clr
  Register #(.width(32)) x15_a5 (.D(in_r15), .en(WE_15), .clk(in_6), .Q(out_r15));  // open: clr
  Register #(.width(32)) x23_s7 (.D(in_r23), .en(WE_23), .clk(in_6), .Q(out_r23));  // open: clr
  Register #(.width(32)) x31_t6 (.D(in_r31), .en(WE_31), .clk(in_6), .Q(out_r31));  // open: clr
  Register #(.width(32)) x8_s0 (.D(in_r8), .en(WE_8), .clk(in_6), .Q(out_r8));  // open: clr
  Register #(.width(32)) x16_a6 (.D(in_r16), .en(WE_16), .clk(in_6), .Q(out_r16));  // open: clr
  Register #(.width(32)) x24_s8 (.D(in_r24), .en(WE_24), .clk(in_6), .Q(out_r24));  // open: clr
  Decoder #(.select(5)) decoder_1 (
    .out1(WE_1), .out2(WE_2), .out3(WE_3), .out4(WE_4), .out5(WE_5), .out6(WE_6), .out7(WE_7), .out8(WE_8),
    .out9(WE_9), .out10(WE_10), .out11(WE_11), .out12(WE_12), .out13(WE_13), .out14(WE_14), .out15(WE_15),
    .out16(WE_16), .out17(WE_17), .out18(WE_18), .out19(WE_19), .out20(WE_20), .out21(WE_21), .out22(WE_22),
    .out23(WE_23), .out24(WE_24), .out25(WE_25), .out26(WE_26), .out27(WE_27), .out28(WE_28), .out29(WE_29),
    .out30(WE_30), .out31(WE_31), .sel(in_3), .en(in_5));  // open: out0

  // Other names for the same wires on the sheet: CLK = in_6; reg1[4:0] = in_1; reg1_data[31:0] = Outputs;
  //   reg2[4:0] = in_2; reg2_data[31:0] = out_8; reg_write[4:0] = in_3; reg_write_data[31:0] = in_4; WE = in_5

  // Notes on the sheet:
  //   I/O
  //   Inputs
  //   Register Reading
  //   Register Writing
endmodule

module ALU (
  input  [31:0] in_1,
  input  [31:0] in_2,
  input  [3:0] in_3,
  output [31:0] Outputs,
  output [3:0] out_5
);

  wire and_2_out, and_3_out, comparator_1_lt, comparator_3_lt, not_1_out, not_2_out, not_3_out;
  wire [31:0] o_add, o_and, o_div, o_mul, o_mulh, o_or, o_rem, o_sll, o_slt, o_sltu, o_sra, o_srl, o_sub,
       o_xor;

  Multiplexer #(.select(4), .width(32)) multiplexer_1 (
    .in0(o_add), .in1(o_sub), .in2(o_and), .in3(o_or), .in4(o_xor), .in5(o_sll), .in6(o_srl), .in7(o_sra),
    .in8(o_mul), .in9(o_mulh), .in10(o_div), .in11(o_rem), .in12(o_slt), .in13(o_sltu), .in14(in_2),
    .out(Outputs), .sel(in_3));  // open: in15
  Adder #(.width(32)) adder_1 (.a(in_1), .b(in_2), .out(o_add), .cout(out_5[0]));  // open: cin
  Subtractor #(.width(32)) subtractor_1 (.a(in_1), .b(in_2), .out(o_sub));  // open: bin, bout
  assign o_and = in_1 & in_2;  // AND_Gate and_1, 32 bits wide
  assign o_or = in_1 | in_2;  // OR_Gate or_1, 32 bits wide
  assign o_xor = in_1 ^ in_2;  // XOR_Gate xor_1, 32 bits wide
  Shifter #(.width(32)) shifter_1 (.in(in_1), .\dist (in_2[4:0]), .out(o_sll));
  assign o_slt = {{31{comparator_1_lt}}, comparator_1_lt};  // Bit_Extender bit_extender_1
  Comparator #(.width(32)) comparator_1 (.a(in_1), .b(in_2), .lt(comparator_1_lt));  // open: gt, eq
  Comparator #(.width(32)) comparator_2 (.a(Outputs), .b({32{1'b0}}), .eq(out_5[2]), .lt(out_5[3]));  // open: gt
  not not_1 (not_1_out, in_1[31]);
  not not_2 (not_2_out, in_2[31]);
  not not_3 (not_3_out, Outputs[31]);
  and and_2 (and_2_out, in_1[31], in_2[31], not_3_out);
  and and_3 (and_3_out, not_1_out, not_2_out, Outputs[31]);
  Comparator #(.mode("unsigned"), .width(32)) comparator_3 (.a(in_1), .b(in_2), .lt(comparator_3_lt));  // open: gt, eq
  or or_2 (out_5[1], and_2_out, and_3_out);
  Shifter #(.shift("lr"), .width(32)) shifter_2 (.in(in_1), .\dist (in_2[4:0]), .out(o_srl));
  Shifter #(.shift("ar"), .width(32)) shifter_3 (.in(in_1), .\dist (in_2[4:0]), .out(o_sra));
  Multiplier #(.width(32)) multiplier_1 (.a(in_1), .b(in_2), .out(o_mul));  // open: cin, cout
  Multiplier #(.width(32)) multiplier_2 (.a(in_1), .b(in_2), .cout(o_mulh));  // open: out, cin
  Divider #(.width(32)) divider_1 (.a(in_1), .b(in_2), .out(o_div));  // open: upper, rem
  Divider #(.width(32)) divider_2 (.a(in_1), .b(in_2), .rem(o_rem));  // open: out, upper
  assign o_sltu = {{31{comparator_3_lt}}, comparator_3_lt};  // Bit_Extender bit_extender_2

  // Other names for the same wires on the sheet: C = out_5[0]; NZVC[3:0] = out_5; V = out_5[1]; Z = out_5[2];
  //   N = out_5[3]; o_mov[31:0] = in_2; Y[31:0] = in_2; OP[3:0] = in_3; result[31:0] = Outputs; X[31:0] = in_1

  // Notes on the sheet:
  //   0
  //   1
  //   2
  //   3
  //   4
  //   5
  //   6
  //   7
  //   8
  //   9
  //   A
  //   B
  //   C
  //   D
  //   E
  //   I/O
  //   Operation Selection
  //   Inputs
  //   Operations
endmodule
